# Fritzing sketch ArdEos Actual (saved by Fritzing 0.9.2b)
circuit board: 8.95078cm x 6.68545cm
breadboards: 1

parts:
  C4 = Tantalum Capacitor [capacitance=1μF package="100 mil [THT, tantalum]"]
  C5 = Tantalum Capacitor [capacitance=1μF package="100 mil [THT, tantalum]"]
  C1 = Tantalum Capacitor [capacitance=1μF package="100 mil [THT, tantalum]"]
  C2 = Tantalum Capacitor [capacitance=1μF package="100 mil [THT, tantalum]"]
  C3 = Tantalum Capacitor [capacitance=1μF package="100 mil [THT, tantalum]"]
  U4 = Voltage Regulator - 5V [package="TO220 [THT]"]
  U5 = RS232 Transceiver [package=dil16]
  C6 = Ceramic Capacitor [capacitance=100nF package="100 mil [THT, multilayer]"]
  C7 = Ceramic Capacitor [capacitance=100nF package="100 mil [THT, multilayer]"]
  Part1 = HUZZAH ESP8266 Breakout
  J5 = Screw terminal - 2 pins [package=THT]
  J4 = screw terminal, 4 pins

nets:
  N1: C4.-, U5.V-
  GND: C4.+, C5.-, C3.-, U4.GND, U5.GND, C6.0, C7.0, Part1.GND, J5.pin2, J4.pin2
  VCC: C5.+, U5.VCC, Part1.3.3V
  N2: C1.-, U5.C1-
  N3: C1.+, U5.C1+
  N4: C2.-, U5.C2-
  N5: C2.+, U5.C2+
  N6: C3.+, U5.V+
  N7: U4.input_voltage, C7.1, J5.pin1, J4.pin1
  N8: U4.output_voltage, C6.1, Part1.VBAT
  N9: U5.T1IN, Part1.TXD
  N10: U5.R1OUT, Part1.RXD_5V
  N11: U5.R1IN, J4.pin4
  N12: U5.T1OUT, J4.pin3

notes:
  +12v
  gnd
  tx
  rx
  HUZZAH
  MAX232
  Ard120 v0.2
  www.richard-williamson.com

custom parts:
  HUZZAH ESP8266 Breakout: The ESP8266 processor from Espressif is an 80 MHz microcontroller with a full WiFi front-end (both as client and access point) and TCP/IP stack with DNS support as well.
